// Logisim project 4 Bit Universal Shift Register - Version B.circ as structural Verilog: 1 circuit, main circuit main
module main (
  input  CLEAR,
  input  LOAD,
  input  PRESET,
  input  [1:0] S1_S0,
  input  ENABLE,
  input  SERIAL_IN,
  input  SERIAL,
  input  P0,
  input  P3,
  input  P2,
  input  P1,
  output Q4,
  output Q3,
  output Q2,
  output Q0
);

  wire CLK_out, d_ff_1_p2, d_ff_2_p2, d_ff_4_p2, multiplexer_3_p5;

  Clock CLK (.out(CLK_out));
  // D_Flip_Flop d_ff_1: pin names not known; wires that end beside it: CLK_out, d_ff_1_p2, PRESET, LOAD, CLEAR, Q4
  // Multiplexer #(.select(2)) multiplexer_1: pin names not known; wires that end beside it: S1_S0, Q4, SERIAL_IN, d_ff_1_p2, Q3, P0
  // D_Flip_Flop d_ff_2: pin names not known; wires that end beside it: CLK_out, d_ff_2_p2, PRESET, LOAD, CLEAR, Q3
  // Multiplexer #(.select(2)) multiplexer_2: pin names not known; wires that end beside it: ENABLE, S1_S0, Q3, Q4, d_ff_2_p2, Q2, P3
  // Multiplexer #(.select(2)) multiplexer_3: pin names not known; wires that end beside it: ENABLE, S1_S0, Q2, Q3, multiplexer_3_p5, Q0, P2
  // D_Flip_Flop d_ff_3: pin names not known; wires that end beside it: CLK_out, multiplexer_3_p5, PRESET, LOAD, CLEAR, Q2
  // D_Flip_Flop d_ff_4: pin names not known; wires that end beside it: CLK_out, d_ff_4_p2, PRESET, LOAD, CLEAR, Q0
  // Multiplexer #(.select(2)) multiplexer_4: pin names not known; wires that end beside it: ENABLE, S1_S0, Q0, Q2, d_ff_4_p2, SERIAL, P1

  // Notes on the sheet:
  //   Universal Shift Register - Version B
  //   Parallel Inputs
  //   4 Bit Universal Shift Register - Version B
endmodule
