// Logisim project 4 Bit Universal Shift Register - Version D (1).circ as structural Verilog: 1 circuit, main circuit main
module main (
  input  CLEAR,
  input  LOAD,
  input  PRESET,
  input  [1:0] S1_S0,
  input  ENABLE,
  input  SERIAL_IN,
  input  SERIAL,
  input  P0,
  input  P3,
  input  P2,
  input  P1,
  output Q4,
  output Q3,
  output Q2,
  output Q0
);

  wire CLK_out, multiplexer_1_out, multiplexer_2_out, multiplexer_3_out, multiplexer_4_out;

  Clock CLK (.out(CLK_out));
  Multiplexer #(.select(2)) multiplexer_1 (
    .in0(Q4), .in1(SERIAL_IN), .in2(Q3), .in3(P0), .out(multiplexer_1_out), .sel(S1_S0), .en(ENABLE));
  D_Flip_Flop d_ff_1 (
    .clk(CLK_out), .D(multiplexer_1_out), .Q(Q4), .preset(PRESET), .en(LOAD), .reset(CLEAR));  // open: Qn
  D_Flip_Flop d_ff_2 (
    .clk(CLK_out), .D(multiplexer_2_out), .Q(Q3), .preset(PRESET), .en(LOAD), .reset(CLEAR));  // open: Qn
  Multiplexer #(.select(2)) multiplexer_2 (
    .in0(Q3), .in1(Q4), .in2(Q2), .in3(P3), .out(multiplexer_2_out), .sel(S1_S0), .en(ENABLE));
  Multiplexer #(.select(2)) multiplexer_3 (
    .in0(Q2), .in1(Q3), .in2(Q0), .in3(P2), .out(multiplexer_3_out), .sel(S1_S0), .en(ENABLE));
  D_Flip_Flop d_ff_3 (
    .clk(CLK_out), .D(multiplexer_3_out), .Q(Q2), .preset(PRESET), .en(LOAD), .reset(CLEAR));  // open: Qn
  D_Flip_Flop d_ff_4 (
    .clk(CLK_out), .D(multiplexer_4_out), .Q(Q0), .preset(PRESET), .en(LOAD), .reset(CLEAR));  // open: Qn
  Multiplexer #(.select(2)) multiplexer_4 (
    .in0(Q0), .in1(Q2), .in2(SERIAL), .in3(P1), .out(multiplexer_4_out), .sel(S1_S0), .en(ENABLE));

  // Notes on the sheet:
  //   Version D - alternate layout
  //   Universal Shift Register
  //   Parallel Inputs
  //   4 Bit Universal Shift Register - Version D
endmodule
